// Logisim project hw4.circ as structural Verilog: 6 circuits, main circuit main
module main (
);

  RAM ram_1 ();  // open: addr, data, sel, clk, ld, clr
  tedi_regfile tedi_regfile_1 ();  // open: rd, data_in, reset, clk, write_enable, rs1, rs2, out_8, out_9
  ROM rom_1 ();  // open: addr, data
  tedi_ALU tedi_alu_1 ();  // open: A, B, optype, data_out
endmodule

module tedi_adder (
  input  sub,
  input  [15:0] A,
  input  [15:0] B,
  output ovf,
  output [15:0] result
);

  wire one_bit_add_1_out, one_bit_add_2_out, one_bit_add_3_out, one_bit_add_4_out, one_bit_add_5_out,
       one_bit_add_6_out, one_bit_add_7_out, one_bit_add_8_out, one_bit_add_9_out, one_bit_add_10_out,
       one_bit_add_11_out, one_bit_add_12_out, one_bit_add_13_out, one_bit_add_14_out, one_bit_add_15_out,
       one_bit_add_16_out, xor_1_out, xor_2_out, xor_3_out, xor_4_out, xor_5_out, xor_6_out, xor_7_out,
       xor_8_out, xor_9_out, xor_10_out, xor_11_out, xor_12_out, xor_13_out, xor_14_out, xor_15_out,
       xor_16_out;

  one_bit_add one_bit_add_1 (
    .a(xor_1_out), .b(B[15]), .out(one_bit_add_1_out), .in(one_bit_add_2_out), .sum(result[15]));
  xor xor_1 (xor_1_out, A[15], sub);
  one_bit_add one_bit_add_2 (
    .a(xor_2_out), .b(B[14]), .out(one_bit_add_2_out), .in(one_bit_add_3_out), .sum(result[14]));
  xor xor_2 (xor_2_out, A[14], sub);
  one_bit_add one_bit_add_3 (
    .a(xor_3_out), .b(B[13]), .out(one_bit_add_3_out), .in(one_bit_add_4_out), .sum(result[13]));
  xor xor_3 (xor_3_out, A[13], sub);
  xor xor_4 (xor_4_out, A[12], sub);
  one_bit_add one_bit_add_4 (
    .a(xor_4_out), .b(B[12]), .out(one_bit_add_4_out), .in(one_bit_add_5_out), .sum(result[12]));
  xor xor_5 (xor_5_out, A[11], sub);
  one_bit_add one_bit_add_5 (
    .a(xor_5_out), .b(B[11]), .out(one_bit_add_5_out), .in(one_bit_add_6_out), .sum(result[11]));
  one_bit_add one_bit_add_6 (
    .a(xor_6_out), .b(B[10]), .out(one_bit_add_6_out), .in(one_bit_add_7_out), .sum(result[10]));
  xor xor_6 (xor_6_out, A[10], sub);
  xor xor_7 (xor_7_out, A[9], sub);
  one_bit_add one_bit_add_7 (.a(xor_7_out), .b(B[9]), .out(one_bit_add_7_out), .in(one_bit_add_8_out), .sum(result[9]));
  one_bit_add one_bit_add_8 (.a(xor_8_out), .b(B[8]), .out(one_bit_add_8_out), .in(one_bit_add_9_out), .sum(result[8]));
  xor xor_8 (xor_8_out, A[8], sub);
  xor xor_9 (xor_9_out, A[7], sub);
  one_bit_add one_bit_add_9 (
    .a(xor_9_out), .b(B[7]), .out(one_bit_add_9_out), .in(one_bit_add_10_out), .sum(result[7]));
  xor xor_10 (xor_10_out, A[6], sub);
  one_bit_add one_bit_add_10 (
    .a(xor_10_out), .b(B[6]), .out(one_bit_add_10_out), .in(one_bit_add_11_out), .sum(result[6]));
  one_bit_add one_bit_add_11 (
    .a(xor_11_out), .b(B[5]), .out(one_bit_add_11_out), .in(one_bit_add_12_out), .sum(result[5]));
  xor xor_11 (xor_11_out, A[5], sub);
  xor xor_12 (xor_12_out, A[4], sub);
  one_bit_add one_bit_add_12 (
    .a(xor_12_out), .b(B[4]), .out(one_bit_add_12_out), .in(one_bit_add_13_out), .sum(result[4]));
  xor xor_13 (xor_13_out, A[3], sub);
  one_bit_add one_bit_add_13 (
    .a(xor_13_out), .b(B[3]), .out(one_bit_add_13_out), .in(one_bit_add_14_out), .sum(result[3]));
  one_bit_add one_bit_add_14 (
    .a(xor_14_out), .b(B[2]), .out(one_bit_add_14_out), .in(one_bit_add_15_out), .sum(result[2]));
  xor xor_14 (xor_14_out, A[2], sub);
  xor xor_15 (xor_15_out, A[1], sub);
  one_bit_add one_bit_add_15 (
    .a(xor_15_out), .b(B[1]), .out(one_bit_add_15_out), .in(one_bit_add_16_out), .sum(result[1]));
  xor xor_16 (xor_16_out, A[0], sub);
  one_bit_add one_bit_add_16 (.a(xor_16_out), .b(B[0]), .out(one_bit_add_16_out), .in(sub), .sum(result[0]));
  xor xor_17 (ovf, one_bit_add_1_out, one_bit_add_2_out);
endmodule

module one_bit_add (
  input  a,
  input  b,
  input  in,
  output out,
  output sum
);

  wire and_1_out, and_2_out, xor_1_out;

  and and_1 (and_1_out, b, a);
  xor xor_1 (xor_1_out, a, b);
  or or_1 (out, and_1_out, and_2_out);
  and and_2 (and_2_out, xor_1_out, in);
  xor xor_2 (sum, in, xor_1_out);
endmodule

module tedi_register (
  input  [15:0] data_in,
  input  reset,
  input  clk,
  input  write_enable,
  output [15:0] data_out
);

  wire and_1_out;

  and and_1 (and_1_out, clk, write_enable);
  D_Flip_Flop d_ff_1 (.D(data_in[0]), .clk(and_1_out), .Q(data_out[0]), .reset(reset));  // open: Qn, preset
  D_Flip_Flop d_ff_2 (.D(data_in[1]), .clk(and_1_out), .Q(data_out[1]), .reset(reset));  // open: Qn, preset
  D_Flip_Flop d_ff_3 (.D(data_in[2]), .clk(and_1_out), .Q(data_out[2]), .reset(reset));  // open: Qn, preset
  D_Flip_Flop d_ff_4 (.D(data_in[3]), .clk(and_1_out), .Q(data_out[3]), .reset(reset));  // open: Qn, preset
  D_Flip_Flop d_ff_5 (.D(data_in[4]), .clk(and_1_out), .Q(data_out[4]), .reset(reset));  // open: Qn, preset
  D_Flip_Flop d_ff_6 (.D(data_in[5]), .clk(and_1_out), .Q(data_out[5]), .reset(reset));  // open: Qn, preset
  D_Flip_Flop d_ff_7 (.D(data_in[6]), .clk(and_1_out), .Q(data_out[6]), .reset(reset));  // open: Qn, preset
  D_Flip_Flop d_ff_8 (.D(data_in[7]), .clk(and_1_out), .Q(data_out[7]), .reset(reset));  // open: Qn, preset
  D_Flip_Flop d_ff_9 (.D(data_in[8]), .clk(and_1_out), .Q(data_out[8]), .reset(reset));  // open: Qn, preset
  D_Flip_Flop d_ff_10 (.D(data_in[9]), .clk(and_1_out), .Q(data_out[9]), .reset(reset));  // open: Qn, preset
  D_Flip_Flop d_ff_11 (.D(data_in[10]), .clk(and_1_out), .Q(data_out[10]), .reset(reset));  // open: Qn, preset
  D_Flip_Flop d_ff_12 (.D(data_in[11]), .clk(and_1_out), .Q(data_out[11]), .reset(reset));  // open: Qn, preset
  D_Flip_Flop d_ff_13 (.D(data_in[12]), .clk(and_1_out), .Q(data_out[12]), .reset(reset));  // open: Qn, preset
  D_Flip_Flop d_ff_14 (.D(data_in[13]), .clk(and_1_out), .Q(data_out[13]), .reset(reset));  // open: Qn, preset
  D_Flip_Flop d_ff_15 (.D(data_in[14]), .clk(and_1_out), .Q(data_out[14]), .reset(reset));  // open: Qn, preset
  D_Flip_Flop d_ff_16 (.D(data_in[15]), .clk(and_1_out), .Q(data_out[15]), .reset(reset));  // open: Qn, preset

  // Other names for the same wires on the sheet: bit8 = data_in[8]; bit9 = data_in[9]; bit10 = data_in[10];
  //   bit11 = data_in[11]; bit12 = data_in[12]; bit13 = data_in[13]; bit14 = data_in[14]; bit15 = data_in[15]
endmodule

module tedi_regfile (
  input  [2:0] rd,
  input  [15:0] data_in,
  input  reset,
  input  [2:0] rs1,
  input  clk,
  input  write_enable,
  input  [2:0] rs2,
  output [15:0] out_8,
  output [15:0] out_9
);

  wire reg1, reg2, reg3, reg4, reg5, reg6, reg7;
  wire [15:0] out_reg1, out_reg2, out_reg3, out_reg4, out_reg5, out_reg6, out_reg7;

  Decoder #(.select(3)) decoder_1 (
    .out1(reg1), .out2(reg2), .out3(reg3), .out4(reg4), .out5(reg5), .out6(reg6), .out7(reg7), .sel(rd),
    .en(write_enable));  // open: out0
  tedi_register tedi_register_1 (.data_in(data_in), .reset(reset), .clk(clk), .write_enable(reg1), .data_out(out_reg1));
  tedi_register tedi_register_2 (.data_in(data_in), .reset(reset), .clk(clk), .write_enable(reg2), .data_out(out_reg2));
  tedi_register tedi_register_3 (.data_in(data_in), .reset(reset), .clk(clk), .write_enable(reg3), .data_out(out_reg3));
  tedi_register tedi_register_4 (.data_in(data_in), .reset(reset), .clk(clk), .write_enable(reg4), .data_out(out_reg4));
  tedi_register tedi_register_5 (.data_in(data_in), .reset(reset), .clk(clk), .write_enable(reg5), .data_out(out_reg5));
  tedi_register tedi_register_6 (.data_in(data_in), .reset(reset), .clk(clk), .write_enable(reg6), .data_out(out_reg6));
  tedi_register tedi_register_7 (.data_in(data_in), .reset(reset), .clk(clk), .write_enable(reg7), .data_out(out_reg7));
  Multiplexer #(.select(3), .width(16), .enable("false")) multiplexer_1 (
    .in0({16{1'b0}}), .in1(out_reg1), .in2(out_reg2), .in3(out_reg3), .in4(out_reg4), .in5(out_reg5),
    .in6(out_reg6), .in7(out_reg7), .out(out_8), .sel(rs1));
  Multiplexer #(.select(3), .width(16), .enable("false")) multiplexer_2 (
    .in0({16{1'b0}}), .in1(out_reg1), .in2(out_reg2), .in3(out_reg3), .in4(out_reg4), .in5(out_reg5),
    .in6(out_reg6), .in7(out_reg7), .out(out_9), .sel(rs2));
endmodule

module tedi_ALU (
  input  [15:0] A,
  input  [15:0] B,
  input  [2:0] optype,
  output [15:0] data_out
);

  wire [15:0] and_1_out, not_1_out, or_1_out, tedi_adder_1_result;

  tedi_adder tedi_adder_1 (.A(A), .B(B), .sub(optype[0]), .result(tedi_adder_1_result));  // open: ovf
  assign or_1_out = A | B;  // OR_Gate or_1, 16 bits wide
  assign and_1_out = A & B;  // AND_Gate and_1, 16 bits wide
  assign not_1_out = ~A;  // NOT_Gate not_1, 16 bits wide
  Multiplexer #(.select(3), .width(16), .enable("false")) multiplexer_1 (
    .in0(tedi_adder_1_result), .in1(tedi_adder_1_result), .in2(or_1_out), .in3(and_1_out), .in6(not_1_out),
    .out(data_out), .sel(optype));  // open: in4, in5, in7

  // Other names for the same wires on the sheet: sub = optype[0]

  // Notes on the sheet:
  //   001 - subtract
  //   010 - or
  //   011 - and
  //   000 - add
  //   110 - not A
  //   101 - left shift A with B
  //   100 - righst shift A with B
endmodule
